# Fritzing sketch HBridge-1.0 (saved by Fritzing 0.9.0b)
circuit board: 7cm x 5cm

parts:
  MB = DC Motor
  L293D = L293D [package=THT]
  MA = DC Motor
  Arduino_Nano = Arduino Nano (Rev3.0)
  BAT = Battery block 9V
  JP1 = Header 12 [package=1x12_machine-pin-header_lock.004]

nets:
  N1: MB.pin_1, L293D.Out_4_(_Controlled_by_Enable_2_)
  N2: MB.pin_2, L293D.Out_3_(_Controlled_by_Enable_2_)
  EN1: L293D.Enable_1, Arduino_Nano.D10
  IN1: L293D.In_1, Arduino_Nano.D6
  N3: L293D.Out_1_(_Controlled_by_Enable_1_), MA.pin_1
  GND: L293D.0V, BAT.-, JP1.1, JP1.2
  N4: L293D.Out_2_(_Controlled_by_Enable_1_), MA.pin_2
  IN2: L293D.In_2, Arduino_Nano.D7
  9V/VSS+9V: L293D.+Vmotor, Arduino_Nano.VIN, BAT.+
  EN2: L293D.Enable_2, Arduino_Nano.D11/MOSI
  IN3: L293D.In_3, Arduino_Nano.D8
  IN4: L293D.In_4, Arduino_Nano.D9
  VS+5V: L293D.+V, Arduino_Nano.5V, JP1.5, JP1.6
  BSD2: Arduino_Nano.D1/TX, JP1.12
  BSD1: Arduino_Nano.D0/RX, JP1.11
  BSD3: Arduino_Nano.D2, JP1.10
  BSD4: Arduino_Nano.D3, JP1.9
  BSD5: Arduino_Nano.D4, JP1.8
  BSD6: Arduino_Nano.D5, JP1.7
  BSA: Arduino_Nano.A0, JP1.4
  LED1: Arduino_Nano.D13/SCK, JP1.3

notes:
  Vacalourabot HBridge 1.0
  Vacalourabot
  HBridge 1.0
