# Fritzing sketch Steppers-1.0 (saved by Fritzing 0.9.0b)
circuit board: 8.46667cm x 5.64444cm
stripboards: 1

parts:
  VCC+5V = Header 6 [package=1x6_machine-pin-header_lock.004]
  Bluetooth_module_socket = Header 6 [package=1x6_machine-pin-header_lock.004]
  Arduino_socket_1 = Header 12 [package=1x12_machine-pin-header_lock.004]
  Arduino_socket_2 = Header 12 [package=1x12_machine-pin-header_lock.004]
  GND = Header 8 [form="♀ (female)" package=1x8_machine-pin-header]
  Arduino_IO = Header 8 [form="♀ (female)" package=1x8_machine-pin-header]
  ULN2803 = ULN2803 [package=DIP18]
  Stepper_1 = XHP-5 connector [package="xhp connector"]
  Stepper_2 = XHP-5 connector [package="xhp connector"]
  Buzzer = Header 3 [part_number=Buzzer package=molex-1x3_lock]

nets:
  N1: VCC+5V.1, VCC+5V.2, VCC+5V.3, VCC+5V.4, VCC+5V.5, VCC+5V.6, Bluetooth_module_socket.5, Arduino_socket_2.4
  N2: Bluetooth_module_socket.2, Arduino_socket_1.1
  N3: Bluetooth_module_socket.3, Arduino_socket_1.2
  N4: Bluetooth_module_socket.4, Arduino_socket_1.4, ULN2803.0V, Buzzer.1
  N5: Arduino_socket_1.5, ULN2803.In_8
  N6: Arduino_socket_1.6, ULN2803.In_7
  N7: Arduino_socket_1.7, ULN2803.In_6
  N8: Arduino_socket_1.8, ULN2803.In_5
  N9: Arduino_socket_1.9, ULN2803.In_4
  N10: Arduino_socket_1.10, ULN2803.In_3
  N11: Arduino_socket_1.11, ULN2803.In_2
  N12: Arduino_socket_1.12, ULN2803.In_1
  N13: Arduino_socket_2.1, ULN2803.COM_-_Common, Stepper_1.1, Stepper_2.1
  N14: Arduino_socket_2.2, GND.1, GND.2, GND.3, GND.4, GND.5, GND.6, GND.7, GND.8
  N15: Arduino_socket_2.5, Arduino_IO.1
  N16: Arduino_socket_2.6, Arduino_IO.2
  N17: Arduino_socket_2.7, Arduino_IO.3
  N18: Arduino_socket_2.8, Arduino_IO.4
  N19: Arduino_socket_2.9, Arduino_IO.5
  N20: Arduino_socket_2.10, Arduino_IO.6
  N21: Arduino_socket_2.11, Arduino_IO.7
  N22: Arduino_socket_2.12, Arduino_IO.8, Buzzer.3
  N23: ULN2803.Out_8, Stepper_1.2
  N24: ULN2803.Out_7, Stepper_1.3
  N25: ULN2803.Out_6, Stepper_1.4
  N26: ULN2803.Out_5, Stepper_1.5
  N27: ULN2803.Out_4, Stepper_2.2
  N28: ULN2803.Out_3, Stepper_2.3
  N29: ULN2803.Out_2, Stepper_2.4
  N30: ULN2803.Out_1, Stepper_2.5

custom parts:
  Header 6: Header 6 Standard 6-pin 0.1 header.
  Header 8: Header 8 Standard 8-pin 0.1 header.
  ULN2803: ULN2803 8-way Darlington Transistor Driver
  XHP-5 connector: XHP-5 Connector
