# Fritzing sketch botoneira (saved by Fritzing 0.9.0b)
stripboards: 1

parts:
  S2 = Pushbutton [package="[THT]"]
  S1 = Pushbutton [package="[THT]"]
  S6 = Pushbutton [package="[THT]"]
  S5 = Pushbutton [package="[THT]"]
  S3 = Pushbutton [package="[THT]"]
  S4 = Pushbutton [package="[THT]"]
  R2 = Resistor [tolerance=±5% resistance=1k package=THT]
  R4 = Resistor [tolerance=±5% resistance=1k package=THT]
  R6 = Resistor [tolerance=±5% resistance=1k package=THT]
  R7 = Resistor [tolerance=±5% resistance=1k package=THT]
  R8 = Resistor [tolerance=±5% resistance=100k power=1W package=THT]
  R9 = Resistor [tolerance=±5% resistance=1k package=THT]
  R10 = Resistor [tolerance=±5% resistance=1k package=THT]
  R11 = Resistor [tolerance=±5% resistance=1k package=THT]

nets:
  N1: S2.Pin_1, S2.Pin_2, R2.Pin_1, R4.Pin_0
  N2: S2.Pin_3, S2.Pin_4, S1.Pin_3, S1.Pin_4, S6.Pin_3, S6.Pin_4, S5.Pin_1, S5.Pin_2, S3.Pin_3, S3.Pin_4, S4.Pin_3, S4.Pin_4, R8.Pin_1
  N3: S1.Pin_1, S1.Pin_2, R2.Pin_0, R7.Pin_0
  N4: S6.Pin_1, S6.Pin_2, R9.Pin_1, R10.Pin_0
  N5: S5.Pin_3, S5.Pin_4, R4.Pin_1, R11.Pin_1
  N6: S3.Pin_1, S3.Pin_2, R10.Pin_1, R11.Pin_0
  N7: S4.Pin_1, S4.Pin_2, R6.Pin_1, R7.Pin_1
  N8: R6.Pin_0, R8.Pin_0
